# Fritzing sketch dnd (saved by Fritzing 0.9.3b)
breadboards: 1

parts:
  ESP32_-_Back1 = ESP32 - CAM
  S1 = Momentary Switch [package=ksa_sealed_tac_switch]
  S2 = Toggle Switch [package=THT]
  X1 = USB Connectors [package=usb-microb]
  JSerial = male pin header, 6 pins [form="♂ (male)"]
  JLEDs = male pin header, 5 pins [form="♂ (male)"]
  Part1 = LED Matrix - Serial Interface - Red/Green/Blue
  Part2 = LED Matrix - Serial Interface - Red/Green/Blue
  C2 = Electrolytic Capacitor [capacitance=4.7mF voltage=10V package="200 mil [THT, electrolytic]"]

nets:
  N1: ESP32_-_Back1.GPIO14, JLEDs.pin2, Part1.SCK, Part2.SCK
  N2: ESP32_-_Back1.GPIO15, JLEDs.pin4, Part1.CS, Part2.CS
  N3: ESP32_-_Back1.GPIO13, JLEDs.pin3, Part1.MOSI
  GND: ESP32_-_Back1.GND#7, ESP32_-_Back1.GND#16, S1.1, S1.2, X1.GND, JSerial.pin6, JLEDs.pin1, Part1.GND, Part2.GND, C2.-
  VCC: ESP32_-_Back1.5V, S2.L2, Part1.VCC, Part2.VCC, C2.+
  N4: ESP32_-_Back1.GPIO0, S1.3, S1.4
  N5: ESP32_-_Back1.GPIO3_/_RX, JSerial.pin2
  N6: ESP32_-_Back1.GPIO1_/_TX, JSerial.pin1
  N7: S2.COM, X1.VBUS
  N8: Part1.MISO, Part2.MOSI

notes:
  USB Power Bank. 5V. 3500mAH
  .. 6 ..
  <-- Total of 8 displays -->
  Flash Enable button
  Power dip protection
  Serial cable connect header
  Matrix connect header

custom parts:
  ESP32 - CAM: The ESP32-CAM has a very competitive small-size camera module that can operate independently as a minimum system with a footprint of only 27*40.5*4.5mm and a deep sleep current of up to 6mA.
